# Fritzing sketch Hygie_Fritzing_Schematic (saved by Fritzing 0.9.2b)

parts:
  S1 = SWITCH-MOMENTARY-2 [package=tactile-pth-12mm]
  U2 = LIPO-1000mAh [package=lipo-1000]
  S2 = SWITCH-MOMENTARY-2 [package=tactile-pth-12mm]  # not connected
  S3 = SWITCH-MOMENTARY-2 [package=tactile-pth-12mm]  # not connected
  S4 = SWITCH-MOMENTARY-2 [package=tactile-pth-12mm]  # not connected
  Part5 = Bluetooth HC-06 Macho
  GY1 = MPU-6050 Board GY-521 [form="♀ (female)" package=THT]  # not connected
  Part6 = Arduino Pro Mini v13
  R1 = Resistor [tolerance=±5% resistance=100k package="2010 [SMD]"]  # not connected
  R2 = Resistor [tolerance=±5% resistance=100k package="2010 [SMD]"]  # not connected
  R3 = Resistor [tolerance=±5% resistance=100k package="2010 [SMD]"]  # not connected
  R4 = Resistor [tolerance=±5% resistance=100k package="2010 [SMD]"]  # not connected
  TP1 = TP4056 [chip_label=TP4056 package="DIP (Dual Inline) [THT]"]
  Part7 = Real Time Clock Module - DS1307 RTC Breakout Board  # not connected
  S7 = Toggle Switch [package=THT]
  M1 = MAX30102
  LED1 = RGB LED (com. cathode, rgb) [package="5 mm [THT]"]
  U3 = MLX90614 [package=to-39]
  Part8 = FTDI Basic Programmer
  R5 = Resistor [tolerance=±5% resistance=220 package="2010 [SMD]"]
  R7 = Resistor [tolerance=±5% resistance=220 package="2010 [SMD]"]
  R8 = Resistor [tolerance=±5% resistance=220 package="2010 [SMD]"]

nets:
  GND: S1.1, Part5.GND, Part6.GND, TP1.pin6, M1.GND, LED1.common_cathode
  N1: U2.+, TP1.pin4
  N2: U2.-, TP1.pin5
  N3: Part5.TXD, Part6.D2
  N4: Part5.RXD, Part6.D3_PWM
  N5: Part6.D0/TX, Part8.RXI
  N6: Part6.D1/RX, Part8.TXO
  N7: Part6.A5, M1.SCL
  N8: Part6.RAW, S7.COM
  N9: Part6.D10_PWM/SS, R7.Pin_1
  N10: Part6.D9_PWM, R5.Pin_1
  N11: Part6.D8, R8.Pin_1
  N12: TP1.pin3, S7.L1
  N13: M1.SDA, U3.PWM_SDA
  N14: LED1.red_anode, R7.Pin_0
  N15: LED1.green_anode, R5.Pin_0
  N16: LED1.blue_anode, R8.Pin_0

notes:
  4 Buttons
  100kohm Pullup
  MAX30100 Heart Rate
  USB charger
  BOOST 5V
  Bluetooth
  HC-05
  6-DOF sensor
  Arduino Pro Mini
  LED RGB
  FTDI (only to program and DEBUG)
  RTC DS1307
  Non-contact IR Thermometer
  MLX90614
  Lithium Battery
  1000mA

custom parts:
  MPU-6050 Board GY-521: Acelerometro y Giroscopio MPU-6050 Board GY-521
  TP4056: A DIP stand-in part for whatever IC you want. With 6 pins on a 300mil dual inline package (DIP) footprint.
  MAX30102: Oximeter module using the MAX30102 chip. You may wish to read (and check your module) this post on power problems with these modules: https://reedpaper.wordpress.com/2018/08/22/pulse-oximeter-max30100-max30102-how-to-fix-wrong-board/ . As usual, if you want the mounting holes in pcb, you need to drag a hole over the pad in silkscreen to actually drill the hole (by default they are not drilled)
